// Logisim project ADD_1.circ as structural Verilog: 2 circuits, main circuit main
module main (
  input  B,
  input  A,
  input  C,
  output V,
  output S
);

  ADD_1 add_1_1 (.C(C), .A(A), .B(B), .S(S), .V(V));
endmodule

module ADD_1 (
  input  C,
  input  A,
  input  B,
  output S,
  output V
);

  wire and_1_out, and_2_out, or_1_out, xor_1_out;

  xor xor_1 (xor_1_out, A, B);
  or or_1 (or_1_out, B, C);
  and and_1 (and_1_out, B, C);
  and and_2 (and_2_out, or_1_out, A);
  xor xor_2 (S, xor_1_out, C);
  or or_2 (V, and_2_out, and_1_out);
endmodule
