// Logisim project ADD_4.circ as structural Verilog: 3 circuits, main circuit main
module main (
  input  [3:0] A,
  input  [3:0] B,
  input  B_2,
  input  A_2,
  input  C,
  output V,
  output OF,
  output S,
  output [3:0] S_2
);

  ADD_1 add_1_1 (.C(C), .A(A_2), .B(B_2), .S(S), .V(V));
  ADD_4 add_4_1 (.OF(OF), .out_4(S_2), .in_1(A), .in_2(B));
endmodule

module ADD_1 (
  input  C,
  input  A,
  input  B,
  output S,
  output V
);

  wire and_1_out, and_2_out, or_1_out, xor_1_out;

  xor xor_1 (xor_1_out, A, B);
  or or_1 (or_1_out, B, C);
  and and_1 (and_1_out, B, C);
  and and_2 (and_2_out, or_1_out, A);
  xor xor_2 (S, xor_1_out, C);
  or or_2 (V, and_2_out, and_1_out);
endmodule

module ADD_4 (
  input  [3:0] in_1,
  input  [3:0] in_2,
  output OF,
  output [3:0] out_4
);

  wire add_1_2_v, add_1_3_v, add_1_4_v;

  // Probe on in_1
  ADD_1 add_1_1 (.C(add_1_2_v), .A(in_1[3]), .B(in_2[3]), .S(out_4[3]), .V(OF));
  ADD_1 add_1_2 (.C(add_1_3_v), .A(in_1[2]), .B(in_2[2]), .S(out_4[2]), .V(add_1_2_v));
  // Probe on out_4
  ADD_1 add_1_3 (.C(add_1_4_v), .A(in_1[1]), .B(in_2[1]), .S(out_4[1]), .V(add_1_3_v));
  ADD_1 add_1_4 (.C(1'b0), .A(in_1[0]), .B(in_2[0]), .S(out_4[0]), .V(add_1_4_v));
  // Probe on in_2
endmodule
