// Logisim project BCD_7SEG.circ as structural Verilog: 2 circuits, main circuit main
module main (
  input  D,
  input  C,
  input  B,
  input  A
);

  wire bcd_7seg_1_a_2, bcd_7seg_1_b_2, bcd_7seg_1_c_2, bcd_7seg_1_d_2, bcd_7seg_1_e, bcd_7seg_1_f,
       bcd_7seg_1_g;

  BCD_7SEG bcd_7seg_1 (
    .A(D), .B(C), .C(B), .D(A), .A_2(bcd_7seg_1_a_2), .B_2(bcd_7seg_1_b_2), .C_2(bcd_7seg_1_c_2),
    .D_2(bcd_7seg_1_d_2), .G(bcd_7seg_1_g), .E(bcd_7seg_1_e), .F(bcd_7seg_1_f));
  _7_Segment_Display u_7_segment_display_1 (
    .g(bcd_7seg_1_g), .f(bcd_7seg_1_f), .a(bcd_7seg_1_a_2), .b(bcd_7seg_1_b_2), .e(bcd_7seg_1_e),
    .d(bcd_7seg_1_d_2), .c(bcd_7seg_1_c_2));  // open: dp
endmodule

module BCD_7SEG (
  input  A,
  input  B,
  input  C,
  input  D,
  output A_2,
  output B_2,
  output C_2,
  output D_2,
  output G,
  output E,
  output F
);

  wire and_1_out, and_2_out, and_3_out, and_4_out, and_5_out, and_6_out, and_7_out, and_8_out, and_9_out,
       and_10_out, xnor_1_out, xnor_2_out, xor_1_out;

  and and_1 (and_1_out, ~C, ~D);  // AND_Gate
  and and_2 (and_2_out, ~C, B);  // AND_Gate
  and and_3 (and_3_out, B, ~D);  // AND_Gate
  and and_4 (and_4_out, C, ~D);  // AND_Gate
  and and_5 (and_5_out, ~B, ~D);  // AND_Gate
  or or_1 (E, and_4_out, and_5_out);
  or or_2 (F, A, and_1_out, and_2_out, and_3_out);
  or or_3 (C_2, B, ~C, D);  // OR_Gate
  and and_6 (and_6_out, ~B, ~D);  // AND_Gate
  and and_7 (and_7_out, ~B, C);  // AND_Gate
  and and_8 (and_8_out, C, ~D);  // AND_Gate
  and and_9 (and_9_out, B, ~C, D);  // AND_Gate
  or or_4 (D_2, A, and_6_out, and_7_out, and_8_out, and_9_out);
  xor xor_1 (xor_1_out, B, C);
  and and_10 (and_10_out, C, ~D);  // AND_Gate
  xnor xnor_1 (xnor_1_out, B, D);
  xnor xnor_2 (xnor_2_out, C, C);
  or or_5 (A_2, A, C, xnor_1_out);
  or or_6 (B_2, ~B, xnor_2_out);  // OR_Gate
  or or_7 (G, A, xor_1_out, and_10_out);
endmodule
