// Logisim project Contador_Up_Down.circ as structural Verilog: 2 circuits, main circuit Contador Up
module Contador_Up (
  output out_1,
  output out_2,
  output out_3,
  output out_4,
  output out_5
);

  wire clock_1_out, j_k_ff_1_qn, j_k_ff_2_qn, j_k_ff_3_qn, j_k_ff_4_qn;

  Clock clock_1 (.out(clock_1_out));
  J_K_Flip_Flop j_k_ff_1 (
    .J(1'b1), .clk(clock_1_out), .K(1'b1), .Q(out_1), .Qn(j_k_ff_1_qn));  // open: preset, en, reset
  J_K_Flip_Flop j_k_ff_2 (
    .J(1'b1), .clk(j_k_ff_1_qn), .K(1'b1), .Q(out_2), .Qn(j_k_ff_2_qn));  // open: preset, en, reset
  // Probe on {out_5, out_4, out_3, out_2, out_1}
  J_K_Flip_Flop j_k_ff_3 (
    .J(1'b1), .clk(j_k_ff_2_qn), .K(1'b1), .Q(out_3), .Qn(j_k_ff_3_qn));  // open: preset, en, reset
  J_K_Flip_Flop j_k_ff_4 (
    .J(1'b1), .clk(j_k_ff_3_qn), .K(1'b1), .Q(out_4), .Qn(j_k_ff_4_qn));  // open: preset, en, reset
  J_K_Flip_Flop j_k_ff_5 (.J(1'b1), .clk(j_k_ff_4_qn), .K(1'b1), .Q(out_5));  // open: Qn, preset, en, reset
endmodule

module Contador_Down (
  output out_1,
  output out_2,
  output out_3,
  output out_4
);

  wire clock_1_out;

  Clock clock_1 (.out(clock_1_out));
  J_K_Flip_Flop j_k_ff_1 (.J(1'b1), .clk(clock_1_out), .K(1'b1), .Q(out_1));  // open: Qn, preset, en, reset
  // Probe on {out_4, out_3, out_2, out_1}
  J_K_Flip_Flop j_k_ff_2 (.J(1'b1), .clk(out_1), .K(1'b1), .Q(out_2));  // open: Qn, preset, en, reset
  J_K_Flip_Flop j_k_ff_3 (.J(1'b1), .clk(out_2), .K(1'b1), .Q(out_3));  // open: Qn, preset, en, reset
  J_K_Flip_Flop j_k_ff_4 (.J(1'b1), .clk(out_3), .K(1'b1), .Q(out_4));  // open: Qn, preset, en, reset
endmodule
